# Fritzing sketch pi and BMP180 (saved by Fritzing 0.9.3b)

parts:
  Raspberry_Pi1 = Raspberry Pi B+
  Part1 = Adafruit BMP180

nets:
  3V3: Raspberry_Pi1.3v3, Part1.+3V3
  N1: Raspberry_Pi1.GPIO2, Part1.SDA
  N2: Raspberry_Pi1.GPIO3, Part1.SCL
  GND: Raspberry_Pi1.GND, Part1.GND

custom parts:
  Adafruit BMP180: This precision sensor from Bosch is the best low-cost sensing solution for measuring barometric pressure and temperature. Because pressure changes with altitude you can also use it as an altimeter! The sensor is soldered onto a PCB with a 3.3V regulator, I2C level shifter and pull-up resistors on the I2C pins. The BMP180 is the next-generation of sensors from Bosch, and replaces the BMP085.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
