# Fritzing sketch pi and MMA8452 (saved by Fritzing 0.9.3b)

parts:
  Raspberry_Pi_1 = Raspberry Pi 3 [part_number=RPI-3-V1.2]
  3-Axis_Accelerometer1 = 3-Axis Accelerometer Breakout - MMA8452Q

nets:
  3V3: Raspberry_Pi_1.3v3, 3-Axis_Accelerometer1.3.3V
  N1: Raspberry_Pi_1.GPIO2, 3-Axis_Accelerometer1.SDA
  N2: Raspberry_Pi_1.GPIO3, 3-Axis_Accelerometer1.SCL
  GND: Raspberry_Pi_1.GND, 3-Axis_Accelerometer1.GND
