# Fritzing sketch pi and MPL3115A2 (saved by Fritzing 0.9.3b)

parts:
  Raspberry_Pi_1 = Raspberry Pi 3 [part_number=RPI-3-V1.2]
  Part2 = MPL3115A2 I2C Barometric Pressure, Altitude, Temperature Sensor

nets:
  3V3: Raspberry_Pi_1.3v3, Part2.+3V3
  N1: Raspberry_Pi_1.GPIO2, Part2.SDA
  N2: Raspberry_Pi_1.GPIO3, Part2.SCL
  GND: Raspberry_Pi_1.GND, Part2.GND

custom parts:
  MPL3115A2 I2C Barometric Pressure, Altitude, Temperature Sensor: This pressure sensor from Freescale is a great low-cost sensing solution for precision measurement of barometric pressure and altitude. The MPL3115A2 has a typical 1.5 Pascal resolution, which can resolve altitude at 0.3 meters (compare to the BMP180 which can do 0.17m). It has some upsides compared to the BMP180, such as interrupt outputs for ultra-low power usage, and its also a heck of a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
