# Fritzing sketch pi and adxl345 (saved by Fritzing 0.9.3b)

parts:
  Part1 = Adafruit ADXL345 [part_number="Adafruit #1231"]
  Raspberry_Pi1 = Raspberry Pi 2

nets:
  3.3V: Part1.3.3V, Raspberry_Pi1.3v3
  GND: Part1.GND, Raspberry_Pi1.GND
  N1: Part1.SDA/SDIO, Raspberry_Pi1.GPIO2
  N2: Part1.SCL, Raspberry_Pi1.GPIO3

custom parts:
  Adafruit ADXL345: Filling out our accelerometer offerings, we now have the really lovely digital ADXL345 from Analog Devices, a triple-axis accelerometer with digital I2C and SPI interface breakout. We added an on-board 3.3V regulator and logic-level shifting circuitry, making it a perfect choice for interfacing with any 3V or 5V microcontroller such as the Arduino. The sensor has three axes of measurements, X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
