# Fritzing sketch pi and mag3110 (saved by Fritzing 0.9.3b)

parts:
  Raspberry_Pi1 = Raspberry Pi B+
  Part1 = MAG3110

nets:
  3V3: Raspberry_Pi1.3v3, Part1.VCC
  N1: Raspberry_Pi1.GPIO2, Part1.SDA
  N2: Raspberry_Pi1.GPIO3, Part1.SCL
  GND: Raspberry_Pi1.GND, Part1.GND

custom parts:
  MAG3110: Sparkfun MAG3110 Breakout
