# Fritzing sketch pi and max7219 (saved by Fritzing 0.9.2b)

parts:
  Part1 = Matrix LED de 8x8 basada en MAX7219
  Raspberry_Pi1 = Raspberry Pi B rev2

nets:
  VCC: Part1.VCC, Raspberry_Pi1.5V
  GND: Part1.GND, Raspberry_Pi1.GND
  N1: Part1.CS, Raspberry_Pi1.GPIO_8
  N2: Part1.CLK, Raspberry_Pi1.GPIO_11
  N3: Part1.DIN, Raspberry_Pi1.GPIO_10
