# Fritzing sketch pi and mcp4725 (saved by Fritzing 0.9.3b)

parts:
  Part1 = Adafruit MCP4725 Breakout Board - 12-Bit DAC [part_number="Adafruit #935"]
  Raspberry_Pi1 = Raspberry Pi B rev2

nets:
  VDD: Part1.VDD, Raspberry_Pi1.3V3
  GND: Part1.GND, Raspberry_Pi1.GND
  N1: Part1.SCL, Raspberry_Pi1.GPIO_3
  N2: Part1.SDA, Raspberry_Pi1.GPIO_2

custom parts:
  Adafruit MCP4725 Breakout Board - 12-Bit DAC: Your microcontroller probably has an ADC (analog -> digital converter) but does it have a DAC (digital -> analog converter)??? Now it can! This breakout board features the easy-to-use MCP4725 12-bit DAC. Control it via I2C and send it the value you want it to output, and the VOUT pin will have it. Great for audio / analog projects, such as when you can't use PWM but need a sine wave or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
