# Fritzing sketch pi and mpu6050 (saved by Fritzing 0.9.3b)

parts:
  GY1 = GY-521 (MPU-6050) [form="♀ (female)" package=THT]
  Raspberry_Pi1 = Raspberry Pi 2

nets:
  N1: GY1.pin1, Raspberry_Pi1.3v3
  N2: GY1.pin2, Raspberry_Pi1.GND
  N3: GY1.pin3, Raspberry_Pi1.GPIO3
  N4: GY1.pin4, Raspberry_Pi1.GPIO2

custom parts:
  GY-521 (MPU-6050): Placa GY-521 basada en conjunto de acelerómetro+giroscopios MPU-6050
