# Fritzing sketch pi and pcf8574 (saved by Fritzing 0.9.3b)
breadboards: 1

parts:
  U1 = PCF8574 [package="DIP16 [THT]"]
  LED1 = LED - 5mm [color="Red (633nm)" package="5 mm [THT]"]
  LED2 = LED - 5mm [color="Red (633nm)" package="5 mm [THT]"]
  Raspberry_Pi2 = Raspberry Pi B rev2

nets:
  N1: U1.A0, U1.A1, U1.A3, U1.GND
  N2: U1.P0, LED1.anode
  N3: U1.P1, LED2.anode
  N4: U1.SCL, Raspberry_Pi2.GPIO_3
  N5: U1.SDA, Raspberry_Pi2.GPIO_2
  VCC: U1.VCC, Raspberry_Pi2.5V
  N6: LED1.cathode, LED2.cathode, Raspberry_Pi2.GND
