# Fritzing sketch pi and si7021 (saved by Fritzing 0.9.3b)

parts:
  Raspberry_Pi_B_rev1 = Raspberry Pi B rev1
  Part1 = Adafruit Si7021 Temp Humidity [part_number="Adafruit #3251"]

nets:
  3V3: Raspberry_Pi_B_rev1.3V3, Part1.+3V3
  N1: Raspberry_Pi_B_rev1.GPIO_0, Part1.SDA
  N2: Raspberry_Pi_B_rev1.GPIO_1, Part1.SCL
  GND: Raspberry_Pi_B_rev1.GND, Part1.GND

custom parts:
  Adafruit Si7021 Temp Humidity: It's summer and you're sweating and your hair's all frizzy and all you really want to know is why the weatherman said this morning that today's relative humidity would max out at a perfectly reasonable 42% when it feels more like 77%. Enter the Si7021 Temperature + Humidity Sensor - the best way to prove the weatherman wrong! This lovely sensor for Silicon labs has ± 3% relative humidity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
