# Fritzing sketch pi and veml6070 (saved by Fritzing 0.9.3b)

parts:
  Part1 = VEML6070 [part_number=VEML6070]
  Raspberry_Pi_1 = Raspberry Pi 3 [part_number=RPI-3-V1.2]

nets:
  VDD: Part1.VDD, Raspberry_Pi_1.3v3
  GND: Part1.GND, Raspberry_Pi_1.GND
  N1: Part1.SCL, Raspberry_Pi_1.GPIO3
  N2: Part1.SDA, Raspberry_Pi_1.GPIO2

custom parts:
  VEML6070: This little sensor is a great way to add UV light sensing to any microcontroller project. The VEML6070 from Vishay has a true UV A light sensor and an I2C-controlled ADC that will take readings and integrate them for you over ~60ms to 500ms.
