# Fritzing sketch pi pwm led (saved by Fritzing 0.9.3b)
breadboards: 1

parts:
  Raspberry_Pi1 = Raspberry Pi B rev2
  R1 = Resistor [tolerance=±5% resistance=470 package=THT]
  LED1 = LED - 5mm [color="Red (633nm)" package="5 mm [THT]"]

nets:
  N1: Raspberry_Pi1.GND, LED1.cathode
  N2: Raspberry_Pi1.GPIO_18, R1.Pin_0
  N3: R1.Pin_1, LED1.anode
