# Fritzing sketch temperature-MCP23017 (saved by Fritzing 0.9.2b)
breadboards: 1

parts:
  Raspberry_Pi1 = Raspberry Pi B rev2
  IC1 = MCP23017 I2C I/O Expander
  R1 = Resistor [tolerance=±5% resistance=220 package=THT]
  LED1 = LED - 5mm [color="Red (633nm)" package="5 mm [THT]"]

nets:
  3V3: Raspberry_Pi1.3V3, IC1.VDD, IC1.RESET
  N1: Raspberry_Pi1.GPIO_2, IC1.SDA
  N2: Raspberry_Pi1.GPIO_3, IC1.SCL
  GND: Raspberry_Pi1.GND, IC1.VSS, IC1.A0, IC1.A1, IC1.A2, LED1.cathode
  N3: IC1.GPA0, R1.Pin_1

custom parts:
  MCP23017 I2C I/O Expander: The MCP23017 uses two i2c pins (these can be shared with other i2c devices), and in exchange gives you 16 general purpose pins. You can set each of 16 pins to be input, output, input with a pullup or open drain. There's even the ability to get an interrupt via an external pin when any of the inputs change so you don't have to keep polling the chip.
