# Fritzing sketch temperature-MCP9808 (saved by Fritzing 0.9.2b)
breadboards: 1

parts:
  Raspberry_Pi1 = Raspberry Pi B rev2
  IC1 = MCP3008 8-channel 10-bit ADC [part_number=MCP3008]
  R1 = Photocell (LDR) [package=THT]
  R2 = Resistor [tolerance=±5% resistance=10k package=THT]

nets:
  N1: Raspberry_Pi1.3V3, IC1.no_name_yet#15, IC1.no_name_yet#16
  N2: Raspberry_Pi1.GND, IC1.no_name_yet#9, IC1.no_name_yet#14, R1.pin_0, R2.Pin_0
  N3: Raspberry_Pi1.GPIO_10, IC1.no_name_yet#11
  N4: Raspberry_Pi1.GPIO_9, IC1.no_name_yet#12
  N5: Raspberry_Pi1.GPIO_11, IC1.no_name_yet#13
  N6: Raspberry_Pi1.GPIO_8, IC1.no_name_yet#10
  N7: IC1.no_name_yet#1, R1.pin_1, R2.Pin_1
